// Logisim project LOOKCARRY.circ as structural Verilog: 1 circuit, main circuit main
module main (
  input  C,
  input  A0,
  input  B0,
  input  A1,
  input  B1,
  input  A2,
  input  B2,
  input  A3,
  input  B3,
  output S0,
  output C1,
  output S1,
  output out_13,
  output out_14,
  output out_15,
  output out_16,
  output out_17
);

  wire and_1_out, and_2_out, and_3_out, and_4_out, and_5_out, and_6_out, and_7_out, and_8_out, and_9_out,
       and_10_out, and_11_out, and_12_out, and_13_out, and_14_out, xor_1_out, xor_2_out, xor_3_out, xor_4_out;

  xor xor_1 (xor_1_out, A0, B0);
  and and_1 (and_1_out, A0, B0);
  xor xor_2 (xor_2_out, A1, B1);
  and and_2 (and_2_out, A1, A1);
  xor xor_3 (xor_3_out, A2, B2);
  and and_3 (and_3_out, A2, B2);
  xor xor_4 (xor_4_out, A3, B3);
  and and_4 (and_4_out, xor_4_out, and_3_out);
  and and_5 (and_5_out, A3, B3);
  and and_6 (and_6_out, and_2_out, xor_3_out);
  and and_7 (and_7_out, C, xor_1_out);
  and and_8 (and_8_out, xor_2_out, and_1_out);
  and and_9 (and_9_out, xor_3_out, xor_2_out, and_1_out);
  and and_10 (and_10_out, xor_3_out, and_2_out, xor_4_out);
  and and_11 (and_11_out, xor_4_out, xor_3_out, xor_2_out, and_2_out);
  and and_12 (and_12_out, xor_2_out, xor_1_out, C);
  and and_13 (and_13_out, xor_3_out, xor_2_out, xor_1_out, C);
  or or_1 (C1, and_7_out, and_1_out);
  or or_2 (out_13, and_12_out, and_8_out, and_2_out);
  xor xor_5 (out_14, out_13, xor_3_out);
  or or_3 (out_15, and_13_out, and_9_out, and_6_out, and_3_out);
  and and_14 (and_14_out, xor_4_out, xor_3_out, xor_2_out, xor_1_out, C);
  xor xor_6 (S0, C, xor_1_out);
  xor xor_7 (S1, C1, xor_2_out);
  xor xor_8 (out_16, out_15, xor_4_out);
  or or_4 (out_17, and_14_out, and_11_out, and_10_out, and_4_out, and_5_out);

  // Notes on the sheet:
  //   1)
  //   P0
  //   G0
  //   P1
  //   G1
  //   P2
  //   G2
  //   P3
  //   G3
  //   C2
  //   S2
  //   C2
  //   S3
  //   C4
endmodule
